# Fritzing sketch Eye2C Board (saved by Fritzing 0.9.3b)
circuit board: 6.50001cm x 2.99999cm
breadboards: 1

parts:
  i2c = double row female pin header, 8 pins [form="♀ (female)"]
  i2c_OLED = Generic female header - 4 pins [form="♀ (female)" package=THT]
  J1 = double row female pin header, 40 pins [form="♀ (female)"]
  R1 = Resistor [tolerance=±5% resistance=330 package=THT]
  R2 = Resistor [tolerance=±5% resistance=470 package=THT]
  R3 = Resistor [tolerance=±5% resistance=330 package=THT]
  R4 = Resistor [tolerance=±5% resistance=470 package=THT]
  R5 = Resistor [tolerance=±5% resistance=330 package=THT]
  R6 = Resistor [tolerance=±5% resistance=470 package=THT]
  R7 = Resistor [tolerance=±5% resistance=330 package=THT]
  R8 = Resistor [tolerance=±5% resistance=470 package=THT]
  HC-SR04_1 = female pin header, 4 pins [form="♀ (female)"]
  HC-SR04_2 = female pin header, 4 pins [form="♀ (female)"]
  HC-SR04_3 = female pin header, 4 pins [form="♀ (female)"]
  HC-SR04_4 = female pin header, 4 pins [form="♀ (female)"]

nets:
  N1: i2c.pin1, i2c.pin8, i2c_OLED.GND, J1.pin5, R2.Pin_0, R4.Pin_0, R6.Pin_0, R8.Pin_0, HC-SR04_1.pin4, HC-SR04_2.pin4, HC-SR04_3.pin4, HC-SR04_4.pin4
  N2: i2c.pin2, i2c.pin7, i2c_OLED.VCC, J1.pin1
  N3: i2c.pin3, i2c.pin6, i2c_OLED.SCL, J1.pin3
  N4: i2c.pin4, i2c.pin5, i2c_OLED.SDA, J1.pin2
  N5: J1.pin6, HC-SR04_1.pin2
  N6: J1.pin7, R1.Pin_1, R2.Pin_1
  N7: J1.pin8, HC-SR04_2.pin2
  N8: J1.pin15, R3.Pin_1, R4.Pin_1
  N9: J1.pin16, HC-SR04_3.pin2
  N10: J1.pin17, R5.Pin_1, R6.Pin_1
  N11: J1.pin18, HC-SR04_4.pin2
  N12: J1.pin19, R7.Pin_1, R8.Pin_1
  N13: J1.pin40, HC-SR04_1.pin1, HC-SR04_2.pin1, HC-SR04_3.pin1, HC-SR04_4.pin1
  N14: R1.Pin_0, HC-SR04_1.pin3
  N15: R3.Pin_0, HC-SR04_2.pin3
  N16: R5.Pin_0, HC-SR04_3.pin3
  N17: R7.Pin_0, HC-SR04_4.pin3

notes:
  gnd
  scl
  sda
  vcc
  v  t  e  g
  Eye2C Board
  https://goo.gl/aAeCfJ

custom parts:
  Generic female header - 4 pins: Generic female header
